# Fritzing sketch Sketch (saved by Fritzing 0.9.3b)
breadboards: 1

parts:
  U1 = 74HC595 [package="DIP16 [THT]"]
  Q1 = PNP-Transistor [package="TO92 [THT]"]
  R1 = Resistor [tolerance=±5% resistance=10k package="2512 [SMD]"]
  R2 = Resistor [tolerance=±5% resistance=1k package="2512 [SMD]"]
  Q2 = PNP-Transistor [package="TO92 [THT]"]
  R3 = Resistor [tolerance=±5% resistance=10k package="2512 [SMD]"]
  R4 = Resistor [tolerance=±5% resistance=1k package="2512 [SMD]"]
  Q3 = PNP-Transistor [package="TO92 [THT]"]
  R5 = Resistor [tolerance=±5% resistance=10k package="2512 [SMD]"]
  R6 = Resistor [tolerance=±5% resistance=1k package="2512 [SMD]"]
  Q4 = PNP-Transistor [package="TO92 [THT]"]
  R7 = Resistor [tolerance=±5% resistance=10k package="2512 [SMD]"]
  R8 = Resistor [tolerance=±5% resistance=1k package="2512 [SMD]"]
  Q5 = PNP-Transistor [package="TO92 [THT]"]
  R9 = Resistor [tolerance=±5% resistance=10k package="2512 [SMD]"]
  R10 = Resistor [tolerance=±5% resistance=1k package="2512 [SMD]"]
  U2 = 7-SEGMENT-4DIGIT [package=7-segment-4digit]
  Q6 = PNP-Transistor [package="TO92 [THT]"]
  R11 = Resistor [tolerance=±5% resistance=10k package="2512 [SMD]"]
  R12 = Resistor [tolerance=±5% resistance=1k package="2512 [SMD]"]
  Q7 = PNP-Transistor [package="TO92 [THT]"]
  R13 = Resistor [tolerance=±5% resistance=10k package="2512 [SMD]"]
  R14 = Resistor [tolerance=±5% resistance=1k package="2512 [SMD]"]
  U3 = 74HC595 [package="DIP16 [THT]"]
  Q8 = PNP-Transistor [package="TO92 [THT]"]
  Q9 = PNP-Transistor [package="TO92 [THT]"]
  Q10 = PNP-Transistor [package="TO92 [THT]"]
  Q11 = PNP-Transistor [package="TO92 [THT]"]
  R15 = Resistor [tolerance=±5% resistance=10k package="2512 [SMD]"]
  R16 = Resistor [tolerance=±5% resistance=10k package="2512 [SMD]"]
  R17 = Resistor [tolerance=±5% resistance=10k package="2512 [SMD]"]
  R18 = Resistor [tolerance=±5% resistance=10k package="2512 [SMD]"]
  R19 = Resistor [tolerance=±5% resistance=1k package="2512 [SMD]"]
  R20 = Resistor [tolerance=±5% resistance=1k package="2512 [SMD]"]
  R21 = Resistor [tolerance=±5% resistance=1k package="2512 [SMD]"]
  R22 = Resistor [tolerance=±5% resistance=1k package="2512 [SMD]"]
  Part1 = Arduino Pro Mini v13

nets:
  N1: U1.Q1, R3.Pin_1
  N2: U1.Q2, R5.Pin_1
  N3: U1.Q3, R7.Pin_1
  N4: U1.Q4, R9.Pin_1
  N5: U1.Q5, R11.Pin_1
  N6: U1.Q6, R13.Pin_1
  GND: U1.GND, U3.GND, Part1.GND
  N7: U1.Q7', U3.DS
  N8: U1.MR, U3.MR, Part1.D4
  N9: U1.SH_CP, U3.SH_CP, Part1.D3_PWM
  N10: U1.ST_CP, U3.ST_CP, Part1.D2
  N11: U1.OE, U3.OE, Part1.D1/RX
  N12: U1.DS, Part1.D0/TX
  N13: U1.Q0, R1.Pin_1
  VCC: U1.VCC, U3.VCC, Q8.E, Q9.E, Q10.E, Q11.E, Part1.VCC
  N14: Q1.E, U2.1
  N15: Q1.B, R1.Pin_0
  N16: Q1.C, R2.Pin_1
  GND_2: R2.Pin_0, R4.Pin_0, R6.Pin_0, R8.Pin_0, R10.Pin_0, R12.Pin_0, R14.Pin_0
  N17: Q2.E, U2.2
  N18: Q2.B, R3.Pin_0
  N19: Q2.C, R4.Pin_1
  N20: Q3.E, U2.3
  N21: Q3.B, R5.Pin_0
  N22: Q3.C, R6.Pin_1
  N23: Q4.E, U2.4
  N24: Q4.B, R7.Pin_0
  N25: Q4.C, R8.Pin_1
  N26: Q5.E, U2.5
  N27: Q5.B, R9.Pin_0
  N28: Q5.C, R10.Pin_1
  N29: U2.6, Q6.E
  N30: U2.7, Q7.E
  N31: U2.13, R19.Pin_0
  N32: U2.14, R21.Pin_0
  N33: U2.15, R20.Pin_0
  N34: U2.16, R22.Pin_0
  N35: Q6.B, R11.Pin_0
  N36: Q6.C, R12.Pin_1
  N37: Q7.B, R13.Pin_0
  N38: Q7.C, R14.Pin_1
  N39: U3.Q1, R18.Pin_1
  N40: U3.Q2, R17.Pin_1
  N41: U3.Q3, R16.Pin_1
  N42: U3.Q0, R15.Pin_1
  N43: Q8.B, R16.Pin_0
  N44: Q8.C, R22.Pin_1
  N45: Q9.B, R15.Pin_0
  N46: Q9.C, R19.Pin_1
  N47: Q10.B, R18.Pin_0
  N48: Q10.C, R21.Pin_1
  N49: Q11.B, R17.Pin_0
  N50: Q11.C, R20.Pin_1
