# Fritzing sketch schema (saved by Fritzing 0.9.3b)
breadboards: 1

parts:
  Part1 = Arduino Uno (Rev3)
  LED1 = smd LED [color="Red (633nm)" package="0805 [SMD]"]
  LED2 = smd LED [color="Red (633nm)" package="0805 [SMD]"]
  LED3 = smd LED [color="Red (633nm)" package="0805 [SMD]"]
  R1 = Resistor [tolerance=±5% resistance=330 package="2010 [SMD]"]
  R2 = Resistor [tolerance=±5% resistance=330 package="2010 [SMD]"]
  R3 = Resistor [tolerance=±5% resistance=330 package="2010 [SMD]"]
  LED4 = smd LED [color="Red (633nm)" package="0805 [SMD]"]
  LED5 = smd LED [color="Red (633nm)" package="0805 [SMD]"]
  LED6 = smd LED [color="Red (633nm)" package="0805 [SMD]"]
  R4 = Resistor [tolerance=±5% resistance=330 package="2010 [SMD]"]
  R5 = Resistor [tolerance=±5% resistance=330 package="2010 [SMD]"]
  R6 = Resistor [tolerance=±5% resistance=330 package="2010 [SMD]"]
  CAR_B = Square Pushbutton
  C1 = Electrolytic Capacitor [capacitance=1µF package="0807 [SMD, electrolytic]"]
  R7 = Resistor [tolerance=±5% resistance=10k package="2010 [SMD]"]
  CAR_A = Square Pushbutton
  C2 = Electrolytic Capacitor [capacitance=1µF package="0807 [SMD, electrolytic]"]
  R8 = Resistor [tolerance=±5% resistance=10k package="2010 [SMD]"]

nets:
  N1: Part1.D10_PWM/SS, LED1.anode
  N2: Part1.D11_PWM/MOSI, LED2.anode
  N3: Part1.D12/MISO, LED3.anode
  N4: Part1.D13/SCK, CAR_A.leg1, C2.+, R8.Pin_0
  N5: Part1.GND, R1.Pin_1, R2.Pin_1, R3.Pin_1, R4.Pin_1, R5.Pin_1, R6.Pin_1, C1.-, R7.Pin_0, CAR_A.leg0, C2.-, R8.Pin_1
  N6: Part1.D2, LED6.anode
  N7: Part1.D3_PWM, LED4.anode
  N8: Part1.D4, LED5.anode
  N9: Part1.D5_PWM, CAR_B.leg0, C1.+, R7.Pin_1
  N10: Part1.5V, CAR_B.leg1
  N11: LED1.cathode, R1.Pin_0
  N12: LED2.cathode, R2.Pin_0
  N13: LED3.cathode, R3.Pin_0
  N14: LED4.cathode, R4.Pin_0
  N15: LED5.cathode, R6.Pin_0
  N16: LED6.cathode, R5.Pin_0
